# Fritzing sketch sonar (saved by Fritzing 0.9.3b)

parts:
  WeMos_D1_Mini1 = WeMos D1 Mini
  Sonar_HC-SR04 = hc-sr04
  HW-373 = TP4056 [chip_label=TP4056 package="DIP (Dual Inline) [THT]"]
  R1 = Resistor [tolerance=±5% resistance=51 package="1206 [SMD]"]
  Laser = LED - 5mm [color="Red (633nm)" package="5 mm [THT]"]
  Servo_1 = Basic Servo
  Servo_2 = Basic Servo
  OLED_1_3'_I2C = OLED 128x64 I2C Monochrome Display
  Buzzer = Piezo Speaker
  R2 = Resistor [tolerance=±5% resistance=100k package="1206 [SMD]"]
  18650_holder1 = 18650 holder [package="DIP (Dual Inline) [THT]"]
  U1 = SWITCH_SPDT [package=kps-1290]

nets:
  VCC: WeMos_D1_Mini1.5V, Sonar_HC-SR04.VCC, HW-373.pin3, Servo_1.vcc, Servo_2.vcc, OLED_1_3'_I2C.VDD, R2.Pin_1
  N1: WeMos_D1_Mini1.A0, R2.Pin_0
  N2: WeMos_D1_Mini1.D0, Laser.anode
  N3: WeMos_D1_Mini1.D1, OLED_1_3'_I2C.SDA
  N4: WeMos_D1_Mini1.D2, OLED_1_3'_I2C.SCK
  N5: WeMos_D1_Mini1.D3, Buzzer.pin2
  N6: WeMos_D1_Mini1.D5, Servo_1.pulse
  N7: WeMos_D1_Mini1.D6, Sonar_HC-SR04.Trig
  N8: WeMos_D1_Mini1.D7, Sonar_HC-SR04.Echo
  N9: WeMos_D1_Mini1.D8, Servo_2.pulse
  GND: WeMos_D1_Mini1.G, Sonar_HC-SR04.GND, HW-373.pin6, R1.Pin_1, Servo_1.gnd, Servo_2.gnd, OLED_1_3'_I2C.GND, Buzzer.pin1
  N10: HW-373.pin4, U1.P
  N11: HW-373.pin5, 18650_holder1.holder_-
  N12: R1.Pin_0, Laser.cathode
  N13: 18650_holder1.holder_+, U1.O

custom parts:
  TP4056: A DIP stand-in part for whatever IC you want. With 6 pins on a 300mil dual inline package (DIP) footprint.
  18650 holder: Акум формата 18650 в холдере
